// Logisim project additionneur_demibit.circ as structural Verilog: 4 circuits, main circuit main
module main (
  input  [3:0] a,
  input  [3:0] b
);

  wire and_1_out, n1bit_1_r1, n1bit_2_r1, n1bit_3_r1, n1bit_4_r1, not_1_out;
  wire [3:0] n1bit_1_s;

  not not_1 (not_1_out, a[0]);
  and and_1 (and_1_out, not_1_out, a[0]);
  _1bit u_1bit_1 (.a(and_1_out), .b(a[0]), .R0(b[0]), .S(n1bit_1_s[0]), .R1(n1bit_1_r1));
  _1bit u_1bit_2 (.a(n1bit_1_r1), .b(a[1]), .R0(b[1]), .S(n1bit_1_s[1]), .R1(n1bit_2_r1));
  _1bit u_1bit_3 (.a(n1bit_2_r1), .b(a[2]), .R0(b[2]), .S(n1bit_1_s[2]), .R1(n1bit_3_r1));
  _1bit u_1bit_4 (.a(n1bit_3_r1), .b(a[3]), .R0(b[3]), .S(n1bit_1_s[3]), .R1(n1bit_4_r1));
  Hex_Digit_Display hex_digit_display_1 (.value(n1bit_1_s));  // open: dp
  LED led_1 (.in(n1bit_4_r1));

  // Notes on the sheet:
  //   c
  //   R
endmodule

module demi_bit (
  input  a,
  input  b,
  output out_3,
  output out_4
);

  xor xor_1 (out_3, a, b);
  and and_1 (out_4, a, b);
endmodule

module _1bit (
  input  a,
  input  b,
  input  R0,
  output S,
  output R1
);

  wire demi_bit_1_out_3, demi_bit_1_out_4, demi_bit_2_out_4;

  demi_bit demi_bit_1 (.a(a), .b(b), .out_3(demi_bit_1_out_3), .out_4(demi_bit_1_out_4));
  demi_bit demi_bit_2 (.a(demi_bit_1_out_3), .b(R0), .out_3(S), .out_4(demi_bit_2_out_4));
  or or_1 (R1, demi_bit_2_out_4, demi_bit_1_out_4);
endmodule

module _4bits (
  input  [3:0] a,
  input  [3:0] b,
  output [3:0] c
);

  wire n1bit_1_r1, n1bit_2_r1, n1bit_3_r1, n1bit_4_r1, not_1_out;

  not not_1 (not_1_out, a[0]);
  and and_1 (a[0], not_1_out, a[0]);
  _1bit u_1bit_1 (.a(a[0]), .b(a[0]), .R0(b[0]), .S(c[0]), .R1(n1bit_1_r1));
  _1bit u_1bit_2 (.a(n1bit_1_r1), .b(a[1]), .R0(b[1]), .S(c[1]), .R1(n1bit_2_r1));
  _1bit u_1bit_3 (.a(n1bit_2_r1), .b(a[2]), .R0(b[2]), .S(c[2]), .R1(n1bit_3_r1));
  _1bit u_1bit_4 (.a(n1bit_3_r1), .b(a[3]), .R0(b[3]), .S(c[3]), .R1(n1bit_4_r1));
  Hex_Digit_Display hex_digit_display_1 (.value(c));  // open: dp
  LED led_1 (.in(n1bit_4_r1));

  // Notes on the sheet:
  //   R
endmodule
