// Logisim project circuit1.circ as structural Verilog: 1 circuit, main circuit main
module main (
  input  a,
  input  b
);

  wire and_1_out, and_2_out, and_3_out, and_4_out, not_1_out, not_2_out, or_1_out;

  not not_1 (not_1_out, a);
  not not_2 (not_2_out, b);
  and and_1 (and_1_out, a, not_2_out);
  and and_2 (and_2_out, not_1_out, b);
  and and_3 (and_3_out, a, b);
  and and_4 (and_4_out, not_2_out, not_1_out);
  or or_1 (or_1_out, and_3_out, and_4_out);
  LED led_1 (.in(and_1_out));
  LED led_2 (.in(and_2_out));
  LED led_3 (.in(or_1_out));

  // Notes on the sheet:
  //   a>b
  //   a<b
  //   a=b
endmodule
